// Logisim project finalProje.circ as structural Verilog
module Subtractor4Bit (
  input  [3:0] A,
  input  [3:0] B,
  input  sub,
  output [3:0] SubResult,
  output carryout
);

  wire fulladder_1_cout, fulladder_2_cout, fulladder_3_cout, xor0_out, xor1_out, xor2_out, xor3_out;

  xor xor0 (xor0_out, B[0], sub);
  xor xor1 (xor1_out, B[1], sub);
  xor xor2 (xor2_out, B[2], sub);
  xor xor3 (xor3_out, B[3], sub);
  FullAdder fulladder_1 (.A(A[0]), .B(xor0_out), .Cin(sub), .Sum(SubResult[0]), .Cout(fulladder_1_cout));
  FullAdder fulladder_2 (.A(A[1]), .B(xor1_out), .Cin(fulladder_1_cout), .Sum(SubResult[1]), .Cout(fulladder_2_cout));
  FullAdder fulladder_3 (.A(A[2]), .B(xor2_out), .Cin(fulladder_2_cout), .Sum(SubResult[2]), .Cout(fulladder_3_cout));
  FullAdder fulladder_4 (.A(A[3]), .B(xor3_out), .Cin(fulladder_3_cout), .Sum(SubResult[3]), .Cout(carryout));
endmodule

module LogicUnit (
  input  [3:0] A,
  input  [3:0] B,
  output [3:0] NOT_Result,
  output [3:0] AND_result,
  output [3:0] OR_Result,
  output [3:0] XOR_Result
);

  not not_1 (NOT_Result[0], A[0]);
  not not_2 (NOT_Result[1], A[1]);
  not not_3 (NOT_Result[2], A[2]);
  not not_4 (NOT_Result[3], A[3]);
  and and_1 (AND_result[0], A[0], B[0]);
  and and_2 (AND_result[1], A[1], B[1]);
  and and_3 (AND_result[2], A[2], B[2]);
  and and_4 (AND_result[3], A[3], B[3]);
  or or_1 (OR_Result[0], A[0], B[0]);
  or or_2 (OR_Result[1], A[1], B[1]);
  or or_3 (OR_Result[2], A[2], B[2]);
  or or_4 (OR_Result[3], A[3], B[3]);
  xor xor_1 (XOR_Result[0], A[0], B[0]);
  xor xor_2 (XOR_Result[1], A[1], B[1]);
  xor xor_3 (XOR_Result[2], A[2], B[2]);
  xor xor_4 (XOR_Result[3], A[3], B[3]);
endmodule

module ALU (
  input  [2:0] OPCODE,
  input  [3:0] A,
  input  [3:0] B,
  output [3:0] result
);

  wire [3:0] adder4bit_1_sum, dec4bit_1_dec_result, inc4bit_1_inc_result, logicunit_1_and_result,
       logicunit_1_or_result, logicunit_1_xor_result, subtractor4bit_1_subresult;

  LogicUnit logicunit_1 (
    .A(A), .B(B), .AND_result(logicunit_1_and_result), .OR_Result(logicunit_1_or_result),
    .XOR_Result(logicunit_1_xor_result));  // open: NOT_Result
  Subtractor4Bit subtractor4bit_1 (.A(A), .B(B), .sub(1'b1), .SubResult(subtractor4bit_1_subresult));  // open: carryout
  INC4Bit inc4bit_1 (.A(A), .INC_Result(inc4bit_1_inc_result));  // open: INC_Carry
  Adder4Bit adder4bit_1 (.A(A), .B(B), .SUM(adder4bit_1_sum));  // open: COUT
  DEC4Bit dec4bit_1 (.A(A), .DEC_Result(dec4bit_1_dec_result));  // open: DEC_Carry
  Multiplexer #(.disabled("Z"), .select(3), .width(4)) multiplexer_1 (
    .in0(adder4bit_1_sum), .in1(subtractor4bit_1_subresult), .in2(inc4bit_1_inc_result),
    .in3(dec4bit_1_dec_result), .in4(4'b0000), .in5(logicunit_1_and_result), .in6(logicunit_1_or_result),
    .in7(logicunit_1_xor_result), .out(result), .sel(OPCODE));
endmodule

module ControlUnit (
  input  LOAD_BTN,
  input  EXECUTE_BTN,
  input  RESET,
  output IDLE,
  output LOAD,
  output EXECUTE,
  output DISPLAY
);

  wire not_1_out, not_2_out, not_3_out;

  not not_1 (not_1_out, LOAD_BTN);
  not not_2 (not_2_out, EXECUTE_BTN);
  not not_3 (not_3_out, RESET);
  and and_1 (IDLE, not_1_out, not_2_out, not_3_out);

  assign DISPLAY = EXECUTE_BTN;
  assign EXECUTE = EXECUTE_BTN;
  assign LOAD = LOAD_BTN;
endmodule

module FullAdder (
  input  A,
  input  B,
  input  Cin,
  output Sum,
  output Cout
);

  wire and_1_out, and_2_out, xor_1_out;

  xor xor_1 (xor_1_out, A, B);
  and and_1 (and_1_out, A, B);
  xor xor_2 (Sum, xor_1_out, Cin);
  and and_2 (and_2_out, xor_1_out, Cin);
  or or_1 (Cout, and_1_out, and_2_out);
endmodule

module Adder4Bit (
  input  [3:0] A,
  input  [3:0] B,
  output [3:0] SUM,
  output COUT
);

  wire fulladder_2_cout, fulladder_3_cout, fulladder_4_cout;

  FullAdder fulladder_1 (.A(A[3]), .B(B[3]), .Cin(fulladder_2_cout), .Sum(SUM[3]), .Cout(COUT));
  FullAdder fulladder_2 (.A(A[2]), .B(B[2]), .Cin(fulladder_3_cout), .Sum(SUM[2]), .Cout(fulladder_2_cout));
  FullAdder fulladder_3 (.A(A[1]), .B(B[1]), .Cin(fulladder_4_cout), .Sum(SUM[1]), .Cout(fulladder_3_cout));
  FullAdder fulladder_4 (.A(A[0]), .B(B[0]), .Cin(1'b0), .Sum(SUM[0]), .Cout(fulladder_4_cout));
endmodule

module INC4Bit (
  input  [3:0] A,
  output [3:0] INC_Result,
  output INC_Carry
);

  Adder4Bit adder4bit_1 (.A(A), .B(4'b0000), .SUM(INC_Result), .COUT(INC_Carry));
endmodule

module DEC4Bit (
  input  [3:0] A,
  output [3:0] DEC_Result,
  output DEC_Carry
);

  // Subtractor4Bit subtractor4bit_1: pin names not known; wires that end beside it: 1'b1, A, 4'b1111, DEC_Result, DEC_Carry
endmodule

module Flag_zero (
  input  [3:0] RESULT,
  output Z
);

  wire or_1_out, or_2_out, or_3_out;

  or or_1 (or_1_out, RESULT[0], RESULT[1]);
  or or_2 (or_2_out, RESULT[2], RESULT[3]);
  or or_3 (or_3_out, or_1_out, or_2_out);
  not not_1 (Z, or_3_out);
endmodule

module Carry_Flag (
  input  COUT,
  output carry
);


  assign carry = COUT;
endmodule

module Flag_sign (
  input  [3:0] Result,
  output Sign
);


  assign Sign = Result[3];
endmodule

module register4bit (
  input  [3:0] D,
  input  LOAD,
  input  CLOCK,
  output [3:0] Q
);

  Register #(.width(4)) register_1 (.D(D), .en(LOAD), .clk(CLOCK), .Q(Q));  // open: clr
endmodule

module Main (
  input  [2:0] OPCODE,
  input  [3:0] A,
  input  LOAD,
  input  CLOCK,
  input  [3:0] B,
  input  RESET
);

  wire [3:0] alu_1_result, RegisterA_q, RegisterB_q, Result_Register_q;

  register4bit RegisterA (.D(A), .LOAD(LOAD), .CLOCK(CLOCK), .Q(RegisterA_q));
  register4bit RegisterB (.D(B), .LOAD(LOAD), .CLOCK(CLOCK), .Q(RegisterB_q));
  ALU alu_1 (.OPCODE(OPCODE), .A(RegisterA_q), .B(RegisterB_q), .result(alu_1_result));
  register4bit Result_Register (.D(alu_1_result), .LOAD(LOAD), .CLOCK(CLOCK), .Q(Result_Register_q));
  Hex_Digit_Display hex_digit_display_1 (.value(Result_Register_q));  // open: dp
  LED led_1 (.in(Result_Register_q[0]));
  LED led_2 (.in(Result_Register_q[1]));
  LED led_3 (.in(Result_Register_q[2]));
  LED led_4 (.in(Result_Register_q[3]));
endmodule
